# Fritzing sketch schematics (saved by Fritzing 0.8.7b)

parts:
  U1 = NodeMCU V3.0
  Part1 = FC-28 Soil Hygrometer Module
  Part2 = FC-28 Soil Hygrometer Module - Probe
  DHT11_1 = DHT11 module
  F1 = Fan - Ventilador [package=THT]
  U2 = LM2596 step down module
  KY-2 = Keyes Relay [package=THT]
  DC-808_Water_Pump1 = DC-808 Water Pump
  JACK1 = 2.1mm DC Barrel Jack
  KY-3 = Keyes Relay [package=THT]

nets:
  N1: U1.D4, DHT11_1.DATA
  3V3: U1.3V3, DHT11_1.VCC
  GND: U1.GND#6, U1.GND#16, U1.GND#33, DHT11_1.GND, U2.IN-, U2.OUT-, DC-808_Water_Pump1.GND, JACK1.center
  N2: U1.D5, KY-2.signal
  N3: U1.D6, KY-3.signal
  VIN: U1.Vin, Part1.VCC, U2.OUT+
  N4: U1.GND#41, Part1.GND
  N5: U1.A0, Part1.AO
  N6: Part1.POS, Part2.POS
  N7: Part1.NEG, Part2.NEG
  N8: F1.5V, KY-3.C
  N9: U2.IN+, KY-2.NO, JACK1.switch
  N10: KY-2.power, KY-3.power
  N11: KY-2.C, DC-808_Water_Pump1.VCC

custom parts:
  NodeMCU V3.0: ESP8266 based NodeMCU
  FC-28 Soil Hygrometer Module: The FC-28 is a soil hygrometer module that uses the Texas Instruments LM393 comparator chip to provide an analog measurement of soil humidity. The digital output is high when soil moisture is over a certain threshold, as determined by adjusting the potentiometer.
  FC-28 Soil Hygrometer Module - Probe: The FC-28 is a soil hygrometer module that uses the Texas Instruments LM393 comparator chip to provide an analog measurement of soil humidity.
  DHT11 module: DHT11 black pcb module
  Fan - Ventilador: Ventilador de 2 pines, se encuentra comunmente en computadoras de escritorio
  LM2596 step down module: LM2596 DC-DC step down power supply module 3 A.
  Keyes Relay: The Keyes 5V relay module is suitable for SCM development, home appliance control. It uses a 5V~12V TIL control signal which can control DC / AC signal.
  DC-808 Water Pump: Water pump.
  2.1mm DC Barrel Jack: 2.1mm DC Barrel Jack with Thru-Hole Connectors (breadboardable)
